# Fritzing sketch RotaryDecoder (saved by Fritzing 0.9.3b)
circuit board: 8.46667cm x 5.64444cm
breadboards: 1

parts:
  Part1 = Arduino Nano (Rev3.0)
  RE1 = Rotary Encoder [package=THT]

nets:
  N1: Part1.GND, RE1.EncoderPinC
  N2: Part1.D2, RE1.EncoderPinA
  N3: Part1.D3, RE1.EncoderPinB
